// Logisim project S2-T11.circ as structural Verilog: 4 circuits, main circuit main
module main (
  input  SL1,
  input  SL2,
  input  s1L2,
  output O1L1,
  output O2L1,
  output O3L1,
  output O4L1,
  output LEVEL_1_PASSED,
  output O1L2,
  output O2L2,
  output O3L2,
  output O4L2,
  output LEVEL_2_PASSED
);

  wire and_1_out, and_2_out, and_4_out, and_6_out, LFSR1_r1, LFSR1_r2, LFSR1_r3, LFSR1_r4, LFSR2_r1,
       LFSR2_r2, LFSR2_r3, LFSR2_r4;

  LFSR LFSR1 (.SWITCH1(SL1), .R1(LFSR1_r1), .R2(LFSR1_r2), .R3(LFSR1_r3), .R4(LFSR1_r4));
  LFSR LFSR2 (.SWITCH1(SL2), .R1(LFSR2_r1), .R2(LFSR2_r2), .R3(LFSR2_r3), .R4(LFSR2_r4));
  Level1 LEVEL1 (
    .R1L1(LFSR1_r1), .E1L1(1'b1), .R2L1(LFSR1_r2), .E2L1(1'b1), .R3L1(LFSR1_r3), .E3L1(1'b1),
    .R4L1(LFSR1_r4), .E4L1(1'b1), .O1L1(O1L1), .O2L1(O2L1), .O3L1(O3L1), .O4L1(O4L1));
  Level2 LEVEL2 (
    .R1L2(and_1_out), .E1L2(1'b1), .R2L2(and_2_out), .E2L2(1'b1), .R3L2(and_4_out), .E3L2(1'b1),
    .R4L2(and_6_out), .E4L2(1'b1), .s1L2(s1L2), .O1L2(O1L2), .O2L2(O2L2), .O3L2(O3L2), .O4L2(O4L2));
  and and_1 (and_1_out, LFSR2_r1, LEVEL_1_PASSED);
  and and_2 (and_2_out, LFSR2_r2, LEVEL_1_PASSED);
  and and_3 (LEVEL_1_PASSED, O1L1, O2L1, O3L1);
  and and_4 (and_4_out, LFSR2_r3, LEVEL_1_PASSED);
  and and_5 (LEVEL_2_PASSED, O1L2, O2L2);
  and and_6 (and_6_out, LFSR2_r4, LEVEL_1_PASSED);
  LED MISSION_SUCCESSFUL_ABORT (.in(LEVEL_2_PASSED));

  // Notes on the sheet:
  //   INSTRUCTIONS:
  //   1.Input the shifter bits to 01
  //   2.Start by clicking SWITCH-1 for generating random inputs for level-1.
  //   4.Click s1L2 if the user wants to turn on the system O3L2
  //   5.The mission is succesful if all the two levels are passed.
  //   SWITCH-1 for generating random inputs for LEVEL-1
  //   4 BIT random Input for LEVEL-1
  //   Expected bits for LEVEL 1
  //   SWITCH-2 for generating random inputs for LEVEL-2
  //   4 BIT random input for LEVEL-2
  //   Expected bits for LEVEL 2
  //   3.IF LEVEL-1 fails,mission is aborted.If LEVEL-1 is passed then click  on SWITCH 2 to give random input to LEVEL-2.
  //   E1L1
  //   E2L1
  //   E3L1
  //   E4L1
  //   E1L2
  //   E2L2
  //   E3L2
  //   E4L2
  //   corrected outputs for LEVEL-1
  //   FAULT TOLERANCE IN SPACECRAFTS(SMALL SCALE)
  //   corrected outputs for LEVEL-2
  //   TEAM DETAILS 
  //   AALIMA KHAN  231CS201
  //   BUKKA LAHARI 231CS217
  //   BASITHA SADIPIRALA  231CS251
endmodule

module Level2 (
  input  R1L2,
  input  E1L2,
  input  R2L2,
  input  E2L2,
  input  R3L2,
  input  E3L2,
  input  R4L2,
  input  E4L2,
  input  s1L2,
  output O1L2,
  output O2L2,
  output O3L2,
  output O4L2
);

  wire and_2_out, and_3_out, and_5_out, multiplexer_2_out, not_1_out, not_2_out, not_3_out, xor_1_out,
       xor_2_out, xor_3_out, xor_4_out;

  and and_1 (O1L2, not_1_out, 1'b1);
  not not_1 (not_1_out, xor_1_out);
  xor xor_1 (xor_1_out, R1L2, E1L2);
  and and_2 (and_2_out, 1'b1, O2L2);
  Multiplexer multiplexer_1 (.in0(and_3_out), .in1(E2L2), .out(O2L2), .sel(xor_2_out), .en(O1L2));
  xor xor_2 (xor_2_out, and_3_out, E2L2);
  and and_3 (and_3_out, O1L2, R2L2);
  not not_2 (not_2_out, E3L2);
  not not_3 (not_3_out, E4L2);
  LED RED_Terminate (.in(O1L2));
  and and_4 (O3L2, 1'b1, multiplexer_2_out);
  xor xor_3 (xor_3_out, and_5_out, not_2_out);
  and and_5 (and_5_out, and_2_out, R3L2);
  Multiplexer multiplexer_2 (.in0(and_5_out), .in1(not_2_out), .out(multiplexer_2_out), .sel(xor_3_out), .en(s1L2));
  LED GREEN_Level_2_passed (.in(O2L2));
  LED YELLOW_Non_essential_subsystem_is_ON (.in(xor_4_out));
  xor xor_4 (xor_4_out, R4L2, not_3_out);

  assign O4L2 = R4L2;

  // Notes on the sheet:
  //   R1L2:
  //   Incorrectable
  //   R2L2:
  //   R3L2:
  //   R4L2:
  //   RANDOM BITS FOR LEVEL2(INPUT)
  //   Correctable
  //   Correctable
  //   Non-essential  subsystem
  //   subsystem
  //   Crucial
  //   subsystem
  //   Crucial
  //   non-crucial
  //   subsystem
  //   EXPECTED BITS FOR LEVEL 2
  //   GREEN: Can move to other bits for checking
  //   RED:No success
  //   OUTPUT BITS FOR LEVEL 2
endmodule

module LFSR (
  input  SWITCH1,
  output R1,
  output R2,
  output R3,
  output R4
);

  wire xnor_1_out;

  D_Flip_Flop d_ff_1 (.clk(SWITCH1), .D(xnor_1_out), .Q(R1));  // open: Qn, preset, en, reset
  D_Flip_Flop d_ff_2 (.clk(SWITCH1), .D(R1), .Q(R2));  // open: Qn, preset, en, reset
  D_Flip_Flop d_ff_3 (.clk(SWITCH1), .D(R2), .Q(R3));  // open: Qn, preset, en, reset
  D_Flip_Flop d_ff_4 (.clk(SWITCH1), .D(R3), .Q(R4));  // open: Qn, preset, en, reset
  xnor xnor_1 (xnor_1_out, R4, R2);
endmodule

module Level1 (
  input  R1L1,
  input  E1L1,
  input  R2L1,
  input  E2L1,
  input  R3L1,
  input  E3L1,
  input  R4L1,
  input  E4L1,
  output O1L1,
  output O2L1,
  output O3L1,
  output O4L1
);

  wire and_2_out, and_3_out, and_5_out, multiplexer_2_out, not_1_out, not_2_out, xor_1_out, xor_2_out,
       xor_3_out, xor_4_out;

  and and_1 (O1L1, not_1_out, 1'b1);
  not not_1 (not_1_out, xor_1_out);
  xor xor_1 (xor_1_out, R1L1, E1L1);
  and and_2 (and_2_out, 1'b1, O2L1);
  Multiplexer multiplexer_1 (.in0(and_3_out), .in1(E2L1), .out(O2L1), .sel(xor_2_out), .en(O1L1));
  xor xor_2 (xor_2_out, and_3_out, E2L1);
  and and_3 (and_3_out, O1L1, R2L1);
  not not_2 (not_2_out, E4L1);
  LED GREEN_Level_1_passed (.in(O3L1));
  and and_4 (O3L1, 1'b1, multiplexer_2_out);
  Multiplexer multiplexer_2 (.in0(and_5_out), .in1(E3L1), .out(multiplexer_2_out), .sel(xor_3_out), .en(and_2_out));
  xor xor_3 (xor_3_out, and_5_out, E3L1);
  and and_5 (and_5_out, and_2_out, R3L1);
  LED RED_Terminate (.in(O1L1));
  LED YELLOW_Non_essential_subbsystem_is_ON (.in(xor_4_out));
  xor xor_4 (xor_4_out, R4L1, not_2_out);

  assign O4L1 = R4L1;

  // Notes on the sheet:
  //   R1L1:
  //   Incorrectable
  //   R2L1:
  //   R3L1:
  //   R4L1:
  //   RANDOM BITS FOR LEVEL1(INPUT)
  //   Correctable
  //   Correctable
  //   Non-essential  subsystem
  //   subsystem
  //   Crucial
  //   subsystem
  //   Crucial
  //   subsystem
  //   Crucial
  //   EXPECTED BITS FOR LEVEL 1
  //   GREEN: Can move to other bits for checking
  //   RED:No success
  //   OUTPUT BITS FOR LEVEL 1
endmodule
