// Logisim project S2-T11.circ as structural Verilog: 5 circuits, main circuit main
module main (
  input  SL1,
  input  SL2,
  input  s1L2,
  input  [2:0] in_4,
  input  SL3,
  input  s2L3,
  input  s1L3,
  output O1L1,
  output O2L1,
  output O3L1,
  output O4L1,
  output O5L1,
  output LEVEL_1_PASSED,
  output O1L2,
  output O2L2,
  output O3L2,
  output O4L2,
  output O5L2,
  output LEVEL_2_PASSED,
  output O1L3,
  output O2L3,
  output O3L3,
  output O4L3,
  output O5L3,
  output LEVEL_3_PASSED,
  output MISSION_SUCCESFUL
);

  wire and_1_out, and_2_out, and_3_out, and_5_out, and_7_out, and_8_out, and_10_out, and_11_out, and_12_out,
       and_13_out, LFSR1_r1, LFSR1_r2, LFSR1_r3, LFSR1_r4, LFSR1_r5, LFSR2_r1, LFSR2_r2, LFSR2_r3, LFSR2_r4,
       LFSR2_r5, LFSR3_r1, LFSR3_r2, LFSR3_r3, LFSR3_r4, LFSR3_r5;
  wire [0:0] not_1_out;
  wire [4:0] shifter_1_out, shifter_2_out;

  Shifter #(.width(5)) shifter_1 (.in({4'b1111, not_1_out[0]}), .\dist (in_4), .out(shifter_1_out));
  Shifter #(.width(5)) shifter_2 (.in(shifter_1_out), .\dist (in_4), .out(shifter_2_out));
  LFSR LFSR1 (.SWITCH1(SL1), .R1(LFSR1_r1), .R2(LFSR1_r2), .R3(LFSR1_r3), .R4(LFSR1_r4), .R5(LFSR1_r5));
  LFSR LFSR2 (.SWITCH1(SL2), .R1(LFSR2_r1), .R2(LFSR2_r2), .R3(LFSR2_r3), .R4(LFSR2_r4), .R5(LFSR2_r5));
  LFSR LFSR3 (.SWITCH1(SL3), .R1(LFSR3_r1), .R2(LFSR3_r2), .R3(LFSR3_r3), .R4(LFSR3_r4), .R5(LFSR3_r5));
  not not_1 (not_1_out[0], 1'b1);
  Level1 LEVEL1 (
    .R1L1(LFSR1_r1), .E1L1(1'b1), .R2L1(LFSR1_r2), .E2L1(1'b1), .R3L1(LFSR1_r3), .E3L1(1'b1),
    .R4L1(LFSR1_r4), .E4L1(1'b1), .R5L1(LFSR1_r5), .E5L1(not_1_out[0]), .O1L1(O1L1), .O2L1(O2L1),
    .O3L1(O3L1), .O4L1(O4L1), .O5L1(O5L1));
  Level2 LEVEL2 (
    .R1L2(and_1_out), .E1L2(shifter_1_out[4]), .R2L2(and_2_out), .E2L2(shifter_1_out[3]), .R3L2(and_5_out),
    .E3L2(shifter_1_out[2]), .R4L2(and_10_out), .E4L2(shifter_1_out[1]), .s1L2(s1L2), .R5L2(and_12_out),
    .E5L2(shifter_1_out[0]), .O1L2(O1L2), .O2L2(O2L2), .O3L2(O3L2), .O4L2(O4L2), .O5L2(O5L2));
  Level3 level3_1 (
    .R1L3(and_3_out), .E1L3(shifter_2_out[4]), .R2L3(and_7_out), .E2L3(shifter_2_out[3]), .R3L3(and_8_out),
    .E3L3(shifter_2_out[2]), .s2L3(s2L3), .R4L3(and_11_out), .E4L3(shifter_2_out[1]), .s1L3(s1L3),
    .R5L3(and_13_out), .E5L3(shifter_2_out[0]), .O1L3(O1L3), .O2L3(O2L3), .O3L3(O3L3), .O4L3(O4L3),
    .O5L3(O5L3));
  and and_1 (and_1_out, LFSR2_r1, LEVEL_1_PASSED);
  and and_2 (and_2_out, LFSR2_r2, LEVEL_1_PASSED);
  and and_3 (and_3_out, LFSR3_r1, LEVEL_2_PASSED);
  and and_4 (LEVEL_1_PASSED, O1L1, O2L1, O3L1, O4L1);
  and and_5 (and_5_out, LFSR2_r3, LEVEL_1_PASSED);
  and and_6 (LEVEL_2_PASSED, O1L2, O2L2, O3L2);
  and and_7 (and_7_out, LFSR3_r2, LEVEL_2_PASSED);
  and and_8 (and_8_out, LFSR3_r3, LEVEL_2_PASSED);
  and and_9 (LEVEL_3_PASSED, O1L3, O2L3);
  and and_10 (and_10_out, LFSR2_r4, LEVEL_1_PASSED);
  and and_11 (and_11_out, LFSR3_r4, LEVEL_2_PASSED);
  and and_12 (and_12_out, LFSR2_r5, LEVEL_1_PASSED);
  and and_13 (and_13_out, LFSR3_r5, LEVEL_2_PASSED);

  assign MISSION_SUCCESFUL = LEVEL_3_PASSED;

  // Notes on the sheet:
  //   Shifter shifts the bits left by 1
  //   SWITCH-1 for generating random inputs for LEVEL-1
  //   5 BIIT random Input for LEVEL-1
  //   SWITCH-2 for generating random inputs for LEVEL-2
  //   5 Bit random input for LEVEL-2
  //   So, input 001
  //   SWITCH-3 for generating random inputs for LEVEL-3
  //   5 BIT random input for LEVEL-3
  //   Shifter shifts the expected inputs by 1 to the left
  //   INSTRUCTIONS:
  //   LEVEL-3
  //   1.Input the shifter bits to 001
  //   2.Start by clicking SWITCH-1 for generating random inputs for level-1.
  //   4.Click s1L2 if the user wants to turn on the system O4L2
  //   7.The mission is succesful if all the three levels are passed.
  //   5.If LEVEL-2 fails,mission is aborted.,else,click on SWITCH-3 to generate random inputs for LEVEL-3
  //   6.Click on s2L3 and s2L4 if the user wants to turn on the systems O3L3 and O4L3.
  //   The system O4L3 is dependent on O3L3.O4L3 can only be turned on if O3L3 is on.
  //   3.IF LEVEL-1 fails,mission is aborted.If LEVEL-1 is passed then click  on SWITCH 2 to give random input to LEVEL-2.
  //   corrected OUTPUTS for LEVEL-1
  //   FAULT TOLERANCE IN SPACECRAFTS
  //   corrected outputs for LEVEL-2
  //   TEAM DETAILS 
  //   AALIMA KHAN  231CS201
  //   BUKKA LAHARI 231CS217
  //   BASITHA SADIPIRALA  231CS251
  //   CORRECTED OUTPUTS FOR LEVEL-3
endmodule

module Level2 (
  input  R1L2,
  input  E1L2,
  input  R2L2,
  input  E2L2,
  input  R3L2,
  input  E3L2,
  input  R4L2,
  input  E4L2,
  input  s1L2,
  input  R5L2,
  input  E5L2,
  output O1L2,
  output O2L2,
  output O3L2,
  output O4L2,
  output O5L2
);

  wire and_2_out, and_3_out, and_4_out, and_5_out, and_7_out, multiplexer_3_out, not_1_out, not_2_out,
       not_3_out, xor_1_out, xor_2_out, xor_3_out, xor_4_out, xor_5_out;

  and and_1 (O1L2, not_1_out, 1'b1);
  not not_1 (not_1_out, xor_1_out);
  xor xor_1 (xor_1_out, R1L2, E1L2);
  and and_2 (and_2_out, 1'b1, O2L2);
  Multiplexer multiplexer_1 (.in0(and_3_out), .in1(E2L2), .out(O2L2), .sel(xor_2_out), .en(O1L2));
  xor xor_2 (xor_2_out, and_3_out, E2L2);
  and and_3 (and_3_out, O1L2, R2L2);
  not not_2 (not_2_out, E4L2);
  not not_3 (not_3_out, E5L2);
  and and_4 (and_4_out, 1'b1, O3L2);
  Multiplexer multiplexer_2 (.in0(and_5_out), .in1(E3L2), .out(O3L2), .sel(xor_3_out), .en(and_2_out));
  xor xor_3 (xor_3_out, and_5_out, E3L2);
  and and_5 (and_5_out, and_2_out, R3L2);
  LED RED_Terminate (.in(O1L2));
  LED GREEN_Level_2_passed (.in(O3L2));
  and and_6 (O4L2, 1'b1, multiplexer_3_out);
  Multiplexer multiplexer_3 (.in0(and_7_out), .in1(not_2_out), .out(multiplexer_3_out), .sel(xor_4_out), .en(s1L2));
  xor xor_4 (xor_4_out, and_7_out, not_2_out);
  and and_7 (and_7_out, and_4_out, R4L2);
  LED YELLOW_Non_essential_subsystem_is_ON (.in(xor_5_out));
  xor xor_5 (xor_5_out, R5L2, not_3_out);

  assign O5L2 = R5L2;

  // Notes on the sheet:
  //   R1L2:
  //   Incorrectable
  //   R2L2:
  //   R3L2:
  //   R4L2:
  //   R5L1:
  //   RANDOM BITS FOR LEVEL1(INPUT)
  //   Correctable
  //   Correctable
  //   Correctable
  //   Non-essential  subsystem
  //   subsystem
  //   Crucial
  //   subsystem
  //   Crucial
  //   subsystem
  //   Crucial
  //   non-crucial
  //   subsystem
  //   EXPECTED BITS FOR LEVEL 2
  //   GREEN: Can move to other bits for checking
  //   RED:No success
  //   OUTPUT BITS FOR LEVEL 2
endmodule

module Level3 (
  input  R1L3,
  input  E1L3,
  input  R2L3,
  input  E2L3,
  input  R3L3,
  input  E3L3,
  input  s2L3,
  input  R4L3,
  input  E4L3,
  input  s1L3,
  input  R5L3,
  input  E5L3,
  output O1L3,
  output O2L3,
  output O3L3,
  output O4L3,
  output O5L3
);

  wire and_2_out, and_3_out, and_4_out, and_5_out, and_7_out, multiplexer_3_out, not_1_out, not_2_out,
       not_3_out, not_4_out, xor_1_out, xor_2_out, xor_3_out, xor_4_out, xor_5_out;

  and and_1 (O1L3, not_1_out, 1'b1);
  not not_1 (not_1_out, xor_1_out);
  xor xor_1 (xor_1_out, R1L3, E1L3);
  and and_2 (and_2_out, 1'b1, O2L3);
  Multiplexer multiplexer_1 (.in0(and_3_out), .in1(E2L3), .out(O2L3), .sel(xor_2_out), .en(O1L3));
  xor xor_2 (xor_2_out, and_3_out, E2L3);
  and and_3 (and_3_out, O1L3, R2L3);
  not not_2 (not_2_out, E3L3);
  not not_3 (not_3_out, E4L3);
  not not_4 (not_4_out, E5L3);
  and and_4 (and_4_out, 1'b1, O3L3);
  Multiplexer multiplexer_2 (.in0(and_5_out), .in1(not_2_out), .out(O3L3), .sel(xor_3_out), .en(s2L3));
  xor xor_3 (xor_3_out, and_5_out, not_2_out);
  and and_5 (and_5_out, and_2_out, R3L3);
  LED RED_Terminate (.in(O1L3));
  LED GREEN_Level_3_passed (.in(O2L3));
  and and_6 (O4L3, 1'b1, multiplexer_3_out);
  Multiplexer multiplexer_3 (.in0(and_7_out), .in1(not_3_out), .out(multiplexer_3_out), .sel(xor_4_out), .en(s1L3));
  xor xor_4 (xor_4_out, and_7_out, not_3_out);
  and and_7 (and_7_out, and_4_out, R4L3);
  LED YELLOW_Non_essential_subsystem_is_ON (.in(xor_5_out));
  xor xor_5 (xor_5_out, R5L3, not_4_out);

  assign O5L3 = R5L3;

  // Notes on the sheet:
  //   R1L2:
  //   Incorrectable
  //   R2L2:
  //   R3L2:
  //   R4L2:
  //   R5L1:
  //   RANDOM BITS FOR LEVEL3(INPUT)
  //   Correctable
  //   Correctable
  //   Correctable
  //   Non-essential  subsystem
  //   subsystem
  //   Crucial
  //   subsystem
  //   Crucial
  //   non-crucial
  //   non-crucial
  //   subsystem
  //   subsystem
  //   EXPECTED BITS FOR LEVEL 3
  //   GREEN: Can move to other bits for checking
  //   RED:No success
  //   OUTPUT BITS FOR LEVEL 3
endmodule

module LFSR (
  input  SWITCH1,
  output R1,
  output R2,
  output R3,
  output R4,
  output R5
);

  wire xnor_1_out;

  D_Flip_Flop d_ff_1 (.clk(SWITCH1), .D(xnor_1_out), .Q(R1));  // open: Qn, preset, en, reset
  D_Flip_Flop d_ff_2 (.clk(SWITCH1), .D(R1), .Q(R2));  // open: Qn, preset, en, reset
  D_Flip_Flop d_ff_3 (.clk(SWITCH1), .D(R2), .Q(R3));  // open: Qn, preset, en, reset
  D_Flip_Flop d_ff_4 (.clk(SWITCH1), .D(R3), .Q(R4));  // open: Qn, preset, en, reset
  D_Flip_Flop d_ff_5 (.clk(SWITCH1), .D(R4), .Q(R5));  // open: Qn, preset, en, reset
  xnor xnor_1 (xnor_1_out, R5, R3);
endmodule

module Level1 (
  input  R1L1,
  input  E1L1,
  input  R2L1,
  input  E2L1,
  input  R3L1,
  input  E3L1,
  input  R4L1,
  input  E4L1,
  input  R5L1,
  input  E5L1,
  output O1L1,
  output O2L1,
  output O3L1,
  output O4L1,
  output O5L1
);

  wire and_2_out, and_3_out, and_4_out, and_5_out, and_7_out, multiplexer_3_out, not_1_out, xor_1_out,
       xor_2_out, xor_3_out, xor_4_out, xor_5_out;

  and and_1 (O1L1, not_1_out, 1'b1);
  not not_1 (not_1_out, xor_1_out);
  xor xor_1 (xor_1_out, R1L1, E1L1);
  and and_2 (and_2_out, 1'b1, O2L1);
  Multiplexer multiplexer_1 (.in0(and_3_out), .in1(E2L1), .out(O2L1), .sel(xor_2_out), .en(O1L1));
  xor xor_2 (xor_2_out, and_3_out, E2L1);
  and and_3 (and_3_out, O1L1, R2L1);
  and and_4 (and_4_out, 1'b1, O3L1);
  Multiplexer multiplexer_2 (.in0(and_5_out), .in1(E3L1), .out(O3L1), .sel(xor_3_out), .en(and_2_out));
  xor xor_3 (xor_3_out, and_5_out, E3L1);
  and and_5 (and_5_out, and_2_out, R3L1);
  LED RED_Terminate (.in(O1L1));
  LED GREEN_Level_1_passed (.in(O4L1));
  and and_6 (O4L1, 1'b1, multiplexer_3_out);
  Multiplexer multiplexer_3 (.in0(and_7_out), .in1(E4L1), .out(multiplexer_3_out), .sel(xor_4_out), .en(and_4_out));
  xor xor_4 (xor_4_out, and_7_out, E4L1);
  and and_7 (and_7_out, and_4_out, R4L1);
  LED YELLOW_Non_essential_subbsystem_is_ON (.in(xor_5_out));
  xor xor_5 (xor_5_out, R5L1, E5L1);

  assign O5L1 = R5L1;

  // Notes on the sheet:
  //   R1L1:
  //   Incorrectable
  //   R2L1:
  //   R3L1:
  //   R4L1:
  //   R5L1:
  //   RANDOM BITS FOR LEVEL1(INPUT)
  //   Correctable
  //   Correctable
  //   Correctable
  //   Non-essential  subsystem
  //   subsystem
  //   Crucial
  //   subsystem
  //   Crucial
  //   subsystem
  //   Crucial
  //   subsystem
  //   Crucial
  //   EXPECTED BITS FOR LEVEL 1
  //   GREEN: Can move to other bits for checking
  //   RED:No success
  //   OUTPUT BITS FOR LEVEL 1
endmodule
